// Logisim project Master Combination Lock .circ as structural Verilog: 1 circuit, main circuit main
module main (
);

  wire and_1_out, and_2_out, and_3_out, and_4_out, and_5_out, and_6_out, and_7_out, and_8_out, and_9_out,
       Anti_Clockwise_out, clock_1_out, Clockwise_out, comparator_1_eq, comparator_2_eq, comparator_2_gt,
       comparator_2_lt, d_ff_2_q, d_ff_3_q, d_ff_4_qn, Lock_out, multiplexer_2_out, nor_1_out, not_1_out,
       not_2_out, not_3_out, or_1_out, or_2_out, or_3_out, or_4_out, or_5_out, xor_1_out;
  wire [1:0] counter_2_q, counter_3_q, counter_4_q;
  wire [2:2] counter_4_q_2;
  wire [3:0] counter_1_q;
  wire [6:0] multiplexer_1_out;
  wire [6:6] d_ff_1_q;

  Button Lock (.out(Lock_out));
  Button Anti_Clockwise (.out(Anti_Clockwise_out));
  Button Clockwise (.out(Clockwise_out));
  Counter #(.width(4), .max('h9)) counter_1 (
    .load(Anti_Clockwise_out), .count(or_1_out), .Q(counter_1_q), .clk(clock_1_out), .clr(or_5_out));  // open: D, carry
  or or_1 (or_1_out, Anti_Clockwise_out, Clockwise_out);
  Clock clock_1 (.out(clock_1_out));
  nor nor_1 (nor_1_out, counter_1_q[0], counter_1_q[1], counter_1_q[2], counter_1_q[3]);
  and and_1 (and_1_out, counter_1_q[0], counter_1_q[3]);
  D_Flip_Flop d_ff_1 (
    .clk(Anti_Clockwise_out), .D(1'b1), .Q(d_ff_1_q[6]), .reset(Clockwise_out));  // open: Qn, preset, en
  and and_2 (and_2_out, Anti_Clockwise_out, nor_1_out);
  and and_3 (and_3_out, and_1_out, Clockwise_out);
  Counter #(.width(2), .max('h3)) counter_2 (
    .load(and_2_out), .count(or_2_out), .Q(counter_2_q), .clk(clock_1_out), .clr(or_5_out));  // open: D, carry
  or or_2 (or_2_out, and_2_out, and_3_out);
  Hex_Digit_Display hex_digit_display_1 (.value(counter_1_q));  // open: dp
  Hex_Digit_Display hex_digit_display_2 (.value({2'b00, counter_2_q}));  // open: dp
  Comparator #(.width(7)) comparator_1 (
    .a({7{1'b0}}), .b({d_ff_1_q[6], counter_2_q, counter_1_q}), .eq(comparator_1_eq));  // open: gt, lt
  Multiplexer #(.select(2), .width(7)) multiplexer_1 (
    .in0(7'b1011000), .in1({7{1'b0}}), .in2(7'b0010001), .in3(7'b1100000), .out(multiplexer_1_out),
    .sel(counter_4_q));  // open: en
  Counter #(.width(2), .max('h3)) counter_3 (
    .count(comparator_1_eq), .Q(counter_3_q), .clk(comparator_1_eq), .clr(or_4_out));  // open: load, D, carry
  Comparator #(.width(7)) comparator_2 (
    .a({d_ff_1_q[6], counter_2_q, counter_1_q}), .b(multiplexer_1_out), .gt(comparator_2_gt),
    .eq(comparator_2_eq), .lt(comparator_2_lt));
  not not_1 (not_1_out, counter_4_q[1]);
  not not_2 (not_2_out, counter_4_q[0]);
  and and_4 (and_4_out, counter_3_q[0], counter_3_q[1]);
  not not_3 (not_3_out, comparator_2_eq);
  D_Flip_Flop d_ff_2 (.clk(not_3_out), .D(d_ff_1_q[6]), .Q(d_ff_2_q), .en(1'b1));  // open: Qn, preset, reset
  D_Flip_Flop d_ff_3 (.clk(comparator_2_eq), .D(d_ff_1_q[6]), .Q(d_ff_3_q), .en(1'b1));  // open: Qn, preset, reset
  and and_5 (and_5_out, comparator_2_lt, counter_4_q[0], not_1_out);
  or or_3 (or_3_out, and_5_out, and_6_out);
  and and_6 (and_6_out, comparator_2_gt, counter_4_q[1], not_2_out);
  or or_4 (or_4_out, Anti_Clockwise_out, and_4_out);
  xor xor_1 (xor_1_out, d_ff_2_q, d_ff_3_q);
  and and_7 (and_7_out, not_3_out, xor_1_out);
  D_Flip_Flop d_ff_4 (.clk(or_3_out), .D(1'b1), .Qn(d_ff_4_qn), .en(or_3_out), .reset(or_5_out));  // open: Q, preset
  Multiplexer #(.select(2)) multiplexer_2 (
    .in0(and_7_out), .in1(comparator_2_eq), .in2(and_7_out), .in3(comparator_2_eq), .out(multiplexer_2_out),
    .sel(counter_4_q));  // open: en
  and and_8 (and_8_out, d_ff_4_qn, counter_4_q_2[2]);
  Counter #(.width(3), .max('h4)) counter_4 (
    .count(multiplexer_2_out), .Q({counter_4_q_2[2], counter_4_q}), .clk(multiplexer_2_out), .clr(or_5_out));  // open: load, D, carry
  LED Lock_Status (.in(and_8_out));
  and and_9 (and_9_out, Lock_out, and_8_out);
  or or_5 (or_5_out, and_9_out, and_4_out);
endmodule
